# Fritzing sketch touch-to-leds (saved by Fritzing 0.9.3b)
breadboards: 1

parts:
  Part2 = Bare Conductive Touch Board
  Power_plug1 = Power plug
  Part3 = Thermal Printer
  NEOPIXEL1 = Neopixel Strip -- Black (30/m)
  NEOPIXEL2 = Neopixel Strip -- Black (30/m)
  NEOPIXEL3 = Neopixel Strip -- Black (30/m)
  NEOPIXEL4 = Neopixel Strip -- Black (30/m)
  Power_plug2 = Power plug
  R1 = Resistor [tolerance=±5% resistance=500 package=THT]
  R2 = Resistor [tolerance=±5% resistance=500 package=THT]
  R3 = Resistor [tolerance=±5% resistance=500 package=THT]
  R4 = Resistor [tolerance=±5% resistance=500 package=THT]
  C1 = Capacitor Polarized [package=panasonic_c]

nets:
  N1: Part2.D5/SD-CS_PWM_(SD_Card), Part3.TXD
  N2: Part2.D6/D-CS_PWM/A7_(VS1053), Part3.RXD
  GND: Part2.GND, Part3.GND#2, NEOPIXEL1.GND, NEOPIXEL2.GND, NEOPIXEL3.GND, Power_plug2.GND, C1.-
  N3: Part2.D8/MP3-RST/A8_(VS1053), R1.Pin_1
  N4: Part2.D9/MP3-CS_PWM/A9_(VS1053), R2.Pin_1
  N5: Part2.D10_PWM/A10_(MIDI), R3.Pin_1
  N6: Part2.D11_PWM, R4.Pin_1
  N7: Power_plug1.GND, Part3.GND#0
  N8: Power_plug1.VCC, Part3.VH
  N9: NEOPIXEL1.Din, R1.Pin_0
  +5V: NEOPIXEL1.+5V, NEOPIXEL2.+5V, NEOPIXEL3.+5V, NEOPIXEL4.+5V, Power_plug2.VCC, C1.+
  N10: NEOPIXEL2.Din, R2.Pin_0
  N11: NEOPIXEL3.Din, R3.Pin_0
  N12: NEOPIXEL4.Din, R4.Pin_0

notes:
  To Printer
  TX_PIN 6 // Arduino transmit YELLOW WIRE labeled RX on printer
  RX_PIN 5 // Arduino receive GREEN WIRE labeled TX on printer
  To LED Strip
  #define LED_PIN 8

custom parts:
  Neopixel Strip -- Black (30/m): These NeoPixel strips have 30 digitally-addressable pixel LEDs per meter and are very affordable and are only 12.5 mm wide, 10 mm if you remove the strip from the casing.
